# Fritzing sketch Nanocomp_Keypad_underside_v2 (saved by Fritzing 0.9.10b)
stripboards: 1

parts:
  1 = SWITCH-MOMENTARY-2 [package=tactile-pth]
  2 = SWITCH-MOMENTARY-2 [package=tactile-pth]
  3 = SWITCH-MOMENTARY-2 [package=tactile-pth]
  R = SWITCH-MOMENTARY-2 [package=tactile-pth]
  0 = SWITCH-MOMENTARY-2 [package=tactile-pth]
  4 = SWITCH-MOMENTARY-2 [package=tactile-pth]
  5 = SWITCH-MOMENTARY-2 [package=tactile-pth]
  6 = SWITCH-MOMENTARY-2 [package=tactile-pth]
  F = SWITCH-MOMENTARY-2 [package=tactile-pth]
  I = SWITCH-MOMENTARY-2 [package=tactile-pth]
  7 = SWITCH-MOMENTARY-2 [package=tactile-pth]
  8 = SWITCH-MOMENTARY-2 [package=tactile-pth]
  9 = SWITCH-MOMENTARY-2 [package=tactile-pth]
  E = SWITCH-MOMENTARY-2 [package=tactile-pth]
  M = SWITCH-MOMENTARY-2 [package=tactile-pth]
  L = SWITCH-MOMENTARY-2 [package=tactile-pth]
  A = SWITCH-MOMENTARY-2 [package=tactile-pth]
  B = SWITCH-MOMENTARY-2 [package=tactile-pth]
  C = SWITCH-MOMENTARY-2 [package=tactile-pth]
  D = SWITCH-MOMENTARY-2 [package=tactile-pth]
  AB = SWITCH-MOMENTARY-2 [package=tactile-pth]
  G = SWITCH-MOMENTARY-2 [package=tactile-pth]
  CN = SWITCH-MOMENTARY-2 [package=tactile-pth]
  S = SWITCH-MOMENTARY-2 [package=tactile-pth]
  JP1 = Header 10 [package=1x10-2mm-smd]
  RST = SWITCH-MOMENTARY-2 [package=tactile-pth]
  JP2 = Header 10 [package=1x10-2mm-smd]

nets:
  N1: 1.1, 0.1, F.1, E.1, C.1, CN.1, JP1.3, JP2.3
  N2: 1.2, 4.2, 7.2, JP1.9, JP2.9
  N3: 2.1, 5.1, 7.1, 8.1, L.1, A.1, JP1.1, JP2.1
  N4: 2.2, 3.2, 0.2, I.2, JP1.11, JP2.11
  N5: 3.1, 4.1, 6.1, 9.1, B.1, S.1, JP1.2, JP2.2
  N6: R.1, I.1, M.1, D.1, G.1, JP1.4, JP2.4
  N7: R.2, 5.2, 6.2, F.2, JP1.13, JP2.13
  N8: 8.2, 9.2, E.2, M.2, JP1.12, JP2.12
  N9: L.2, G.2, CN.2, S.2, JP1.8, JP2.8
  N10: A.2, B.2, C.2, D.2, JP1.10, JP2.10
  N11: AB.1, JP1.7, JP2.7
  N12: AB.2, JP1.6, RST.2, JP2.6
  N13: JP1.5, RST.1, JP2.5

notes:
  Q3
  Q2
  Q1
  Reset
  GND
  NMI
  PA0
  PA1
  PA2
  PA3
  PA4
  PA5
  Q0

custom parts:
  SWITCH-MOMENTARY-2: Various NO switches- pushbuttons, reed, etc
  Header 10: Header 10 Standard 10-pin 0.1 header. Use with straight break away headers (SKU : PRT-00116), right angle break away headers (PRT-00553), swiss pins (PRT-00743), machine pins (PRT-00117), and female headers (PRT-00115).
