# Fritzing sketch Nanocomp_display_v2 (saved by Fritzing 0.9.10b)
breadboards: 1

parts:
  IC1 = IC, DIP package, 16 pins [chip_label=74LS145]
  U2 = 7-SEGMENT-4DIGIT [package=7-segment-4digit]
  U1 = 7-SEGMENT-4DIGIT [package=7-segment-4digit]
  JP1 = Header 10 [package=1x10-2mm-smd]
  IC2 = IC, DIP package, 18 pins [chip_label=ULN2803A]
  JP2 = Header 10 [package=1x10-2mm-smd]
  R1 = Resistor [tolerance=±5% power=0.25 resistance=5.6k package=THT]
  R2 = Resistor [tolerance=±5% power=0.25 resistance=5.6k package=THT]
  R3 = Resistor [tolerance=±5% power=0.25 resistance=5.6k package=THT]
  R4 = Resistor [tolerance=±5% power=0.25 resistance=5.6k package=THT]
  R5 = Resistor [tolerance=±5% power=0.25 resistance=5.6k package=THT]
  R6 = Resistor [tolerance=±5% power=0.25 resistance=5.6k package=THT]
  R7 = Resistor [tolerance=±5% power=0.25 resistance=5.6k package=THT]
  R8 = Bussed8 Resistor-8 (SIP-9) [tolerance=±5% resistance=220 package=SIP-9]

nets:
  N1: IC1.pin1, JP2.1
  N2: IC1.pin2, JP2.2
  N3: IC1.pin3, JP2.3
  N4: IC1.pin4, JP2.4
  N5: IC1.pin5, U2.Digit1
  N6: IC1.pin6, U2.Digit2
  N7: IC1.pin7, U2.Digit3
  N8: IC1.pin8, IC2.pin9, JP2.6
  N9: IC1.pin9, U2.Digit4
  N10: IC1.pin10, U1.Digit1
  N11: IC1.pin11, U1.Digit2
  N12: IC1.pin12, JP1.4
  N13: IC1.pin13, JP1.3
  N14: IC1.pin14, JP1.2
  N15: IC1.pin15, JP1.1
  N16: IC1.pin16, IC2.pin10, R8.Pin_0
  N17: U2.E, U1.E, IC2.pin7, R8.Pin_7
  N18: U2.D, U1.D, IC2.pin6, R8.Pin_6
  N19: U2.C, U1.C, IC2.pin4, R8.Pin_4
  N20: U2.G, U1.G, IC2.pin2, R8.Pin_2
  N21: U2.B, U1.B, IC2.pin3, R8.Pin_3
  N22: U2.F, U1.F, IC2.pin8, R8.Pin_8
  N23: U2.A, U1.A, IC2.pin5, R8.Pin_5
  N24: JP1.5, JP2.5
  N25: JP1.6, JP2.7
  N26: JP1.7, JP2.8, R1.Pin_1
  N27: JP1.8, JP2.9, R2.Pin_1
  N28: JP1.9, JP2.10, R3.Pin_1
  N29: JP1.10, JP2.11, R4.Pin_1
  N30: JP1.11, JP2.12, R5.Pin_1
  N31: JP1.12, JP2.13, R6.Pin_1
  N32: JP1.13, R7.Pin_1
  N33: IC2.pin1, R8.Pin_1
  N34: IC2.pin11, R7.Pin_0
  N35: IC2.pin12, R6.Pin_0
  N36: IC2.pin13, R5.Pin_0
  N37: IC2.pin14, R4.Pin_0
  N38: IC2.pin15, R3.Pin_0
  N39: IC2.pin16, R2.Pin_0
  N40: IC2.pin17, R1.Pin_0

notes:
  PA5
  PA4
  PA3
  PA2
  PA1
  PA0
  NMI
  GND
  Reset
  PB1
  PB0
  PB2
  PB3
  Q0
  Q1
  Q2
  Q3
  PA6
  x  g  b c  a  d  e  f

custom parts:
  Header 10: Header 10 Standard 10-pin 0.1 header. Use with straight break away headers (SKU : PRT-00116), right angle break away headers (PRT-00553), swiss pins (PRT-00743), machine pins (PRT-00117), and female headers (PRT-00115).
  Bussed8 Resistor-8 (SIP-9): A resistor array is a single package which contains more than one resistor. They are typically used for convenience when several resistors are needed together in the same place in a circuit.
