# Fritzing sketch Nanocomp_display_v3 (saved by Fritzing 0.9.10b)
breadboards: 1

parts:
  IC1 = IC, DIP package, 16 pins [chip_label=74LS145]
  U2 = 7-SEGMENT-4DIGIT [package=7-segment-4digit]
  U1 = 7-SEGMENT-4DIGIT [package=7-segment-4digit]
  IC2 = IC, DIP package, 18 pins [chip_label=ULN2803A]
  R8 = Bussed8 Resistor-8 (SIP-9) [tolerance=±5% resistance=220 package=SIP-9]
  J1 = female pin header, 4 pins [form="♀ (female)"]
  J2 = female pin header, 4 pins [form="♀ (female)"]
  JP2 = Header 8 [package=1x08_smd_alt]
  JP1 = Header 8 [package=1x08_smd_alt]
  J3 = female pin header, 1 pin [form="♀ (female)"]
  J6 = female pin header, 1 pin [form="♀ (female)"]

nets:
  N1: IC1.pin1, J2.pin1
  N2: IC1.pin2, J2.pin2
  N3: IC1.pin3, J2.pin3
  N4: IC1.pin4, J2.pin4
  N5: IC1.pin5, U2.Digit1
  N6: IC1.pin6, U2.Digit2
  N7: IC1.pin7, U2.Digit3
  N8: IC1.pin8, IC2.pin9, JP2.1
  N9: IC1.pin9, U2.Digit4
  N10: IC1.pin10, U1.Digit1
  N11: IC1.pin11, U1.Digit2
  N12: IC1.pin12, J1.pin4
  N13: IC1.pin13, J1.pin3
  N14: IC1.pin14, J1.pin2
  N15: IC1.pin15, J1.pin1
  N16: IC1.pin16, IC2.pin10, R8.Pin_0
  N17: U2.E, U1.E, IC2.pin17, R8.Pin_2
  N18: U2.D, U1.D, IC2.pin15, R8.Pin_4
  N19: U2.C, U1.C, IC2.pin13, R8.Pin_6
  N20: U2.G, U1.G, IC2.pin11, R8.Pin_8
  N21: U2.B, U1.B, IC2.pin12, R8.Pin_7
  N22: U2.F, U1.F, IC2.pin16, R8.Pin_3
  N23: U2.A, U1.A, IC2.pin14, R8.Pin_5
  N24: IC2.pin2, JP1.2
  N25: IC2.pin3, JP2.3, JP1.3
  N26: IC2.pin4, JP2.4, JP1.4
  N27: IC2.pin5, JP2.5, JP1.5
  N28: IC2.pin6, JP2.6, JP1.6
  N29: IC2.pin7, JP2.7, JP1.7
  N30: IC2.pin8, JP2.8, JP1.8
  N31: IC2.pin18, R8.Pin_1
  N32: JP2.2, JP1.1
  N33: J3.pin1, J6.pin1

notes:
  PA5
  PA4
  PA3
  PA2
  PA1
  PA0
  NMI
  GND
  Reset
  PB1
  PB0
  PB2
  PB3
  Q0
  Q1
  Q2
  Q3
  PA6
  5v g  b c  a  d  f  e  x

custom parts:
  Bussed8 Resistor-8 (SIP-9): A resistor array is a single package which contains more than one resistor. They are typically used for convenience when several resistors are needed together in the same place in a circuit.
